// Logisim project Coa-Processor-ALU.circ as structural Verilog: 1 circuit, main circuit main
module main (
  input  [7:0] A,
  input  [7:0] B,
  input  [3:0] S2_S1_S0,
  output [15:0] Y
);

  wire adder_1_cout, adder_2_cout, subtractor_1_bout, subtractor_2_bout;
  wire [2:0] bit_extender_1_out, bit_extender_2_out, bit_extender_3_out, bit_extender_4_out;
  wire [3:0] bit_extender_16_out, bit_extender_16_out_2;
  wire [7:0] adder_1_out, adder_2_out, and_1_out, bit_extender_5_out, bit_extender_6_out, bit_extender_7_out,
       bit_extender_8_out, divider_1_out, divider_1_rem, multiplier_1_cout, multiplier_1_out, not_1_out,
       or_1_out, shifter_1_out, shifter_2_out, shifter_3_out, shifter_4_out, subtractor_1_out,
       subtractor_2_out;
  wire [15:0] bit_extender_9_out, bit_extender_10_out, bit_extender_11_out, bit_extender_12_out,
       bit_extender_13_out, bit_extender_14_out, bit_extender_15_out;

  Bit_Extender #(.out_width(3)) bit_extender_1 (.in(B), .out(bit_extender_1_out));
  Bit_Extender #(.out_width(3)) bit_extender_2 (.in(B), .out(bit_extender_2_out));
  Bit_Extender #(.out_width(3)) bit_extender_3 (.in(B), .out(bit_extender_3_out));
  Bit_Extender #(.out_width(3)) bit_extender_4 (.in(B), .out(bit_extender_4_out));
  Adder adder_1 (.a(A), .b(B), .out(adder_1_out), .cout(adder_1_cout));  // open: cin
  assign bit_extender_5_out = {{7{1'b0}}, adder_1_cout};  // Bit_Extender bit_extender_5
  Subtractor subtractor_1 (.a(A), .b(B), .out(subtractor_1_out), .bout(subtractor_1_bout));  // open: bin
  assign bit_extender_6_out = {{7{1'b0}}, subtractor_1_bout};  // Bit_Extender bit_extender_6
  Multiplier multiplier_1 (.a(A), .b(B), .out(multiplier_1_out), .cout(multiplier_1_cout));  // open: cin
  Divider divider_1 (.a(A), .b(B), .out(divider_1_out), .rem(divider_1_rem));  // open: upper
  Adder adder_2 (.a(A), .b(B), .out(adder_2_out), .cout(adder_2_cout));  // open: cin
  assign bit_extender_7_out = {{7{1'b0}}, adder_2_cout};  // Bit_Extender bit_extender_7
  Subtractor subtractor_2 (.a(A), .b(B), .out(subtractor_2_out), .bout(subtractor_2_bout));  // open: bin
  assign bit_extender_8_out = {{7{1'b0}}, subtractor_2_bout};  // Bit_Extender bit_extender_8
  assign and_1_out = A & B;  // AND_Gate and_1, 8 bits wide
  assign or_1_out = A | B;  // OR_Gate or_1, 8 bits wide
  assign not_1_out = ~A;  // NOT_Gate not_1, 8 bits wide
  Shifter #(.shift("lr")) shifter_1 (.in(A), .\dist (bit_extender_1_out), .out(shifter_1_out));
  Shifter shifter_2 (.in(A), .\dist (bit_extender_2_out), .out(shifter_2_out));
  Shifter #(.shift("rr")) shifter_3 (.in(A), .\dist (bit_extender_3_out), .out(shifter_3_out));
  Shifter #(.shift("rl")) shifter_4 (.in(A), .\dist (bit_extender_4_out), .out(shifter_4_out));
  assign bit_extender_9_out = {{8{1'b0}}, and_1_out};  // Bit_Extender bit_extender_9
  assign bit_extender_10_out = {{8{1'b0}}, or_1_out};  // Bit_Extender bit_extender_10
  assign bit_extender_11_out = {{8{1'b0}}, not_1_out};  // Bit_Extender bit_extender_11
  assign bit_extender_12_out = {{8{1'b0}}, shifter_1_out};  // Bit_Extender bit_extender_12
  assign bit_extender_13_out = {{8{1'b0}}, shifter_2_out};  // Bit_Extender bit_extender_13
  assign bit_extender_14_out = {{8{1'b0}}, shifter_3_out};  // Bit_Extender bit_extender_14
  assign bit_extender_15_out = {{8{1'b0}}, shifter_4_out};  // Bit_Extender bit_extender_15
  Multiplexer #(.select(4), .width(16), .enable("false")) multiplexer_1 (
    .in0({bit_extender_5_out, adder_1_out}), .in1({bit_extender_6_out, subtractor_1_out}),
    .in2({multiplier_1_cout, multiplier_1_out}), .in3({divider_1_rem, divider_1_out}),
    .in4({bit_extender_7_out, adder_2_out}), .in5({bit_extender_8_out, subtractor_2_out}),
    .in6(bit_extender_9_out), .in7(bit_extender_10_out), .in8(bit_extender_11_out),
    .in9(bit_extender_12_out), .in10(bit_extender_13_out), .in11(bit_extender_14_out),
    .in12(bit_extender_15_out), .out(Y), .sel(S2_S1_S0));  // open: in13, in14, in15
  Bit_Extender #(.in_width(16), .out_width(8)) bit_extender_16 (
    .in(Y), .out({bit_extender_16_out_2, bit_extender_16_out}));
  Hex_Digit_Display hex_digit_display_1 (.value(bit_extender_16_out_2));  // open: dp
  Hex_Digit_Display hex_digit_display_2 (.value(bit_extender_16_out));  // open: dp

  // Notes on the sheet:
  //   ALU and with 13 Operations
  //   Add-0
  //   Sub-01
  //   Mul-10
  //   Div-11
  //   Inc-100
  //   Dec-101
  //   Or-111
  //   Not-1000
  //   SHL-1010
  //   ROR-1011
  //   And-110
  //   SHR-1001
  //   ROL-1100
endmodule
