// Logisim project Coa-Processor.circ as structural Verilog: 6 circuits, main circuit main
module main (
  input  [7:0] Pc_in,
  input  in_2
);

  wire Clock, Execute, IR, mem_read, not_1_out, Op_fetch, PC, psw_1_carry, psw_1_even_parity,
       psw_1_half_carry, psw_1_interupt_flag, psw_1_odd_parity, psw_1_overflow, psw_1_sign, psw_1_zero,
       Reset, Write_back;
  wire [3:0] Opcode, RAddress, RD, RS;
  wire [7:0] Accumulator, IA, MAR, PC_point, RA, Reg, Result;
  wire [15:0] RZ;
  wire [19:0] Code_Memory, MBR_q;

  LED led_1 (.in(PC));
  LED led_2 (.in(mem_read));
  control_unit Control_Unit (
    .Clock(Clock), .Reset(Reset), .PC_enable(PC), .Mem_read(mem_read), .IR(IR), .Operand_fetch(Op_fetch),
    .ALU(Execute), .R_W_prime(Write_back));
  LED led_3 (.in(IR));
  LED led_4 (.in(Op_fetch));
  not not_1 (not_1_out, Write_back);
  Register u_RA (.D(Reg), .en(Op_fetch), .Q(RA), .clk(Clock), .clr(Reset));
  LED led_5 (.in(Execute));
  LED led_6 (.in(Write_back));
  pc u_PC (.PC_in(Pc_in), .PC_enable(PC), .Clock(Clock), .Reset(Reset), .PC_out(PC_point));
  Register u_MAR (.D(PC_point), .en(PC), .Q(MAR), .clk(Clock), .clr(Reset));
  ALU alu_1 (.A(RA), .B(IA), .S2_S1_S0(Opcode), .Y(RZ));
  register register_1 (
    .D7D6___________D0(Result), .clk(Clock), .Accumulater(Accumulator), .R_W_prime(not_1_out),
    .S3S2S1S0(RAddress), .Output(Reg));
  ROM #(.dataWidth(20)) rom_1 (.addr(MAR), .data(Code_Memory));  // open: sel
  Register #(.width(16)) u_RZ (.D(RZ), .en(Execute), .Q({Accumulator, Result}), .clk(Clock), .clr(Reset));
  Clock clock_1 (.out(Clock));
  Register #(.width(20)) MBR (.D(Code_Memory), .en(mem_read), .Q(MBR_q), .clk(Clock), .clr(Reset));
  Multiplexer #(.width(4), .enable("false")) multiplexer_1 (.in0(RS), .in1(RD), .out(RAddress), .sel(Write_back));
  Register #(.width(20)) u_IR (.D(MBR_q), .en(IR), .Q({Opcode, RD, RS, IA}), .clk(Clock), .clr(Reset));
  Button B (.out(Reset));
  LED led_7 (.in(Reset));
  Hex_Digit_Display hex_digit_display_1 (.value(RA[3:0]));  // open: dp
  Hex_Digit_Display hex_digit_display_2 (.value(RA[7:4]));  // open: dp
  Hex_Digit_Display hex_digit_display_3 (.value(Opcode));  // open: dp
  Hex_Digit_Display hex_digit_display_4 (.value(PC_point[7:4]));  // open: dp
  Hex_Digit_Display hex_digit_display_5 (.value(PC_point[3:0]));  // open: dp
  Hex_Digit_Display hex_digit_display_6 (.value(IA[7:4]));  // open: dp
  Hex_Digit_Display hex_digit_display_7 (.value(Accumulator[7:4]));  // open: dp
  Hex_Digit_Display hex_digit_display_8 (.value(RD));  // open: dp
  Hex_Digit_Display hex_digit_display_9 (.value(MAR[7:4]));  // open: dp
  Hex_Digit_Display hex_digit_display_10 (.value(IA[3:0]));  // open: dp
  Hex_Digit_Display hex_digit_display_11 (.value(Accumulator[3:0]));  // open: dp
  Hex_Digit_Display hex_digit_display_12 (.value(MAR[3:0]));  // open: dp
  Hex_Digit_Display hex_digit_display_13 (.value(RZ[15:12]));  // open: dp
  Hex_Digit_Display hex_digit_display_14 (.value(RZ[11:8]));  // open: dp
  Hex_Digit_Display hex_digit_display_15 (.value(RZ[7:4]));  // open: dp
  Hex_Digit_Display hex_digit_display_16 (.value(Result[7:4]));  // open: dp
  Hex_Digit_Display hex_digit_display_17 (.value(RS));  // open: dp
  Hex_Digit_Display hex_digit_display_18 (.value(Code_Memory[19:16]));  // open: dp
  Hex_Digit_Display hex_digit_display_19 (.value(Code_Memory[15:12]));  // open: dp
  Hex_Digit_Display hex_digit_display_20 (.value(RZ[3:0]));  // open: dp
  Hex_Digit_Display hex_digit_display_21 (.value(Result[3:0]));  // open: dp
  Hex_Digit_Display hex_digit_display_22 (.value(Code_Memory[11:8]));  // open: dp
  Hex_Digit_Display hex_digit_display_23 (.value(IA[7:4]));  // open: dp
  Hex_Digit_Display hex_digit_display_24 (.value(IA[3:0]));  // open: dp
  Hex_Digit_Display hex_digit_display_25 (.value(Code_Memory[3:0]));  // open: dp
  Hex_Digit_Display hex_digit_display_26 (.value(Code_Memory[7:4]));  // open: dp
  PSW psw_1 (
    .ALU(RZ), .A(RA), .B(IA), .interupt(in_2), .Zero(psw_1_zero), .Overflow(psw_1_overflow),
    .Carry(psw_1_carry), .Sign(psw_1_sign), .Even_Parity(psw_1_even_parity), .odd_parity(psw_1_odd_parity),
    .Half_Carry(psw_1_half_carry), .Interupt_Flag(psw_1_interupt_flag));
  LED Zero (.in(psw_1_zero));
  LED Overflow (.in(psw_1_overflow));
  LED Carry (.in(psw_1_carry));
  LED Sign (.in(psw_1_sign));
  LED Even_Parity (.in(psw_1_even_parity));
  LED Odd_Parity (.in(psw_1_odd_parity));
  LED Half_Carry (.in(psw_1_half_carry));
  LED interrupt (.in(psw_1_interupt_flag));

  // Notes on the sheet:
  //   Instruction Cycles
  //   8bit Processor
  //   Register bank
  //   Code memory
  //   ALU
  //   Operator Buttons
  //   contents of rom_1 (hex, n*v repeats v):
  //   2451f 14506 2780f 3ab02 4de01 5f001 61205 74503 87800 99a02 acd03 bf001 c2304
  //   Register Operand
  //   3- Adressing Format
  //   Opcode
  //   PC-Pointing
  //   Operands and its Result
  //   Immediate Operand
  //   After Write-Back Data stored in registers
  //   Destination-register
  //   Accumulator
  //   MAR-Content
  //   Result
  //   Source-register
  //   Destination-register-Data
  //   Code Memory
  //   Immediate Operand
  //   PSW
endmodule

module pc (
  input  [7:0] PC_in,
  input  PC_enable,
  input  Reset,
  input  Clock,
  output [7:0] PC_out
);

  wire [7:0] adder_1_out;

  Adder adder_1 (.a(PC_in), .b(PC_out), .out(adder_1_out));  // open: cin, cout
  Hex_Digit_Display hex_digit_display_1 (.value(PC_out[7:4]));  // open: dp
  Register register_1 (.D(adder_1_out), .en(PC_enable), .Q(PC_out), .clk(Clock), .clr(Reset));
  Hex_Digit_Display hex_digit_display_2 (.value(PC_out[3:0]));  // open: dp
endmodule

module control_unit (
  input  Clock,
  input  Reset,
  output PC_enable,
  output Mem_read,
  output IR,
  output Operand_fetch,
  output ALU,
  output R_W_prime
);

  wire [2:0] counter_1_q;

  Counter #(.width(3), .max('h7)) counter_1 (.Q(counter_1_q), .clk(Clock), .clr(Reset));  // open: load, D, count, carry
  Decoder #(.select(3), .enable("false")) decoder_1 (
    .out0(PC_enable), .out1(Mem_read), .out2(IR), .out3(Operand_fetch), .out4(ALU), .out5(R_W_prime),
    .sel(counter_1_q));  // open: out6, out7
endmodule

module ALU (
  input  [7:0] A,
  input  [7:0] B,
  input  [3:0] S2_S1_S0,
  output [15:0] Y
);

  wire adder_1_cout, adder_2_cout, subtractor_1_bout, subtractor_2_bout;
  wire [2:0] bit_extender_1_out, bit_extender_2_out, bit_extender_3_out, bit_extender_4_out;
  wire [3:0] bit_extender_16_out, bit_extender_16_out_2;
  wire [7:0] adder_1_out, adder_2_out, and_1_out, bit_extender_5_out, bit_extender_6_out, bit_extender_7_out,
       bit_extender_8_out, divider_1_out, divider_1_rem, multiplier_1_cout, multiplier_1_out, not_1_out,
       or_1_out, shifter_1_out, shifter_2_out, shifter_3_out, shifter_4_out, subtractor_1_out,
       subtractor_2_out;
  wire [15:0] bit_extender_9_out, bit_extender_10_out, bit_extender_11_out, bit_extender_12_out,
       bit_extender_13_out, bit_extender_14_out, bit_extender_15_out;

  Bit_Extender #(.out_width(3)) bit_extender_1 (.in(B), .out(bit_extender_1_out));
  Bit_Extender #(.out_width(3)) bit_extender_2 (.in(B), .out(bit_extender_2_out));
  Bit_Extender #(.out_width(3)) bit_extender_3 (.in(B), .out(bit_extender_3_out));
  Bit_Extender #(.out_width(3)) bit_extender_4 (.in(B), .out(bit_extender_4_out));
  Adder adder_1 (.a(A), .b(B), .out(adder_1_out), .cout(adder_1_cout));  // open: cin
  assign bit_extender_5_out = {{7{1'b0}}, adder_1_cout};  // Bit_Extender bit_extender_5
  Subtractor subtractor_1 (.a(A), .b(B), .out(subtractor_1_out), .bout(subtractor_1_bout));  // open: bin
  assign bit_extender_6_out = {{7{1'b0}}, subtractor_1_bout};  // Bit_Extender bit_extender_6
  Multiplier multiplier_1 (.a(A), .b(B), .out(multiplier_1_out), .cout(multiplier_1_cout));  // open: cin
  Divider divider_1 (.a(A), .b(B), .out(divider_1_out), .rem(divider_1_rem));  // open: upper
  Adder adder_2 (.a(A), .b(B), .out(adder_2_out), .cout(adder_2_cout));  // open: cin
  assign bit_extender_7_out = {{7{1'b0}}, adder_2_cout};  // Bit_Extender bit_extender_7
  Subtractor subtractor_2 (.a(A), .b(B), .out(subtractor_2_out), .bout(subtractor_2_bout));  // open: bin
  assign bit_extender_8_out = {{7{1'b0}}, subtractor_2_bout};  // Bit_Extender bit_extender_8
  assign and_1_out = A & B;  // AND_Gate and_1, 8 bits wide
  assign or_1_out = A | B;  // OR_Gate or_1, 8 bits wide
  assign not_1_out = ~A;  // NOT_Gate not_1, 8 bits wide
  Shifter #(.shift("lr")) shifter_1 (.in(A), .\dist (bit_extender_1_out), .out(shifter_1_out));
  Shifter shifter_2 (.in(A), .\dist (bit_extender_2_out), .out(shifter_2_out));
  Shifter #(.shift("rr")) shifter_3 (.in(A), .\dist (bit_extender_3_out), .out(shifter_3_out));
  Shifter #(.shift("rl")) shifter_4 (.in(A), .\dist (bit_extender_4_out), .out(shifter_4_out));
  assign bit_extender_9_out = {{8{1'b0}}, and_1_out};  // Bit_Extender bit_extender_9
  assign bit_extender_10_out = {{8{1'b0}}, or_1_out};  // Bit_Extender bit_extender_10
  assign bit_extender_11_out = {{8{1'b0}}, not_1_out};  // Bit_Extender bit_extender_11
  assign bit_extender_12_out = {{8{1'b0}}, shifter_1_out};  // Bit_Extender bit_extender_12
  assign bit_extender_13_out = {{8{1'b0}}, shifter_2_out};  // Bit_Extender bit_extender_13
  assign bit_extender_14_out = {{8{1'b0}}, shifter_3_out};  // Bit_Extender bit_extender_14
  assign bit_extender_15_out = {{8{1'b0}}, shifter_4_out};  // Bit_Extender bit_extender_15
  Multiplexer #(.select(4), .width(16), .enable("false")) multiplexer_1 (
    .in0({bit_extender_5_out, adder_1_out}), .in1({bit_extender_6_out, subtractor_1_out}),
    .in2({multiplier_1_cout, multiplier_1_out}), .in3({divider_1_rem, divider_1_out}),
    .in4({bit_extender_7_out, adder_2_out}), .in5({bit_extender_8_out, subtractor_2_out}),
    .in6(bit_extender_9_out), .in7(bit_extender_10_out), .in8(bit_extender_11_out),
    .in9(bit_extender_12_out), .in10(bit_extender_13_out), .in11(bit_extender_14_out),
    .in12(bit_extender_15_out), .out(Y), .sel(S2_S1_S0));  // open: in13, in14, in15
  Bit_Extender #(.in_width(16), .out_width(8)) bit_extender_16 (
    .in(Y), .out({bit_extender_16_out_2, bit_extender_16_out}));
  Hex_Digit_Display hex_digit_display_1 (.value(bit_extender_16_out_2));  // open: dp
  Hex_Digit_Display hex_digit_display_2 (.value(bit_extender_16_out));  // open: dp

  // Notes on the sheet:
  //   ALU and with 13 Operations
  //   Add-0
  //   Sub-01
  //   Mul-10
  //   Div-11
  //   Inc-100
  //   Dec-101
  //   Or-111
  //   Not-1000
  //   SHL-1010
  //   ROR-1011
  //   And-110
  //   SHR-1001
  //   ROL-1100
endmodule

// Reg-Bank
module register (
  input  [7:0] D7D6___________D0,
  input  clk,
  input  [7:0] Accumulater,
  input  R_W_prime,
  input  [3:0] S3S2S1S0,
  output [7:0] Output
);

  wire decoder_1_out0, decoder_1_out1, decoder_1_out2, decoder_1_out3, decoder_1_out4, decoder_1_out5,
       decoder_1_out6, decoder_1_out7, decoder_1_out8, decoder_1_out9, decoder_1_out10, decoder_1_out11,
       decoder_1_out12, decoder_1_out13, decoder_1_out14, decoder_1_out15, not_1_out;
  wire [7:0] register_1_q, register_2_q, register_3_q, register_4_q, register_5_q, register_6_q,
       register_7_q, register_8_q, register_9_q, register_10_q, register_11_q, register_12_q, register_13_q,
       register_14_q, register_15_q, register_16_q;

  not not_1 (not_1_out, R_W_prime);
  Register AC (.D(Accumulater), .en(not_1_out), .clk(clk));  // open: Q, clr
  Hex_Digit_Display hex_digit_display_1 (.value(D7D6___________D0[7:4]));  // open: dp
  Decoder #(.select(4), .disabled(0)) decoder_1 (
    .out0(decoder_1_out0), .out1(decoder_1_out1), .out2(decoder_1_out2), .out3(decoder_1_out3),
    .out4(decoder_1_out4), .out5(decoder_1_out5), .out6(decoder_1_out6), .out7(decoder_1_out7),
    .out8(decoder_1_out8), .out9(decoder_1_out9), .out10(decoder_1_out10), .out11(decoder_1_out11),
    .out12(decoder_1_out12), .out13(decoder_1_out13), .out14(decoder_1_out14), .out15(decoder_1_out15),
    .sel(S3S2S1S0), .en(not_1_out));
  Hex_Digit_Display hex_digit_display_2 (.value(D7D6___________D0[3:0]));  // open: dp
  Register register_1 (.D(D7D6___________D0), .en(decoder_1_out0), .Q(register_1_q), .clk(clk));  // open: clr
  Register register_2 (.D(D7D6___________D0), .en(decoder_1_out1), .Q(register_2_q), .clk(clk));  // open: clr
  Register register_3 (.D(D7D6___________D0), .en(decoder_1_out2), .Q(register_3_q), .clk(clk));  // open: clr
  Register register_4 (.D(D7D6___________D0), .en(decoder_1_out3), .Q(register_4_q), .clk(clk));  // open: clr
  Register register_5 (.D(D7D6___________D0), .en(decoder_1_out4), .Q(register_5_q), .clk(clk));  // open: clr
  Register register_6 (.D(D7D6___________D0), .en(decoder_1_out5), .Q(register_6_q), .clk(clk));  // open: clr
  Register register_7 (.D(D7D6___________D0), .en(decoder_1_out6), .Q(register_7_q), .clk(clk));  // open: clr
  Register register_8 (.D(D7D6___________D0), .en(decoder_1_out7), .Q(register_8_q), .clk(clk));  // open: clr
  Register register_9 (.D(D7D6___________D0), .en(decoder_1_out8), .Q(register_9_q), .clk(clk));  // open: clr
  Register register_10 (.D(D7D6___________D0), .en(decoder_1_out9), .Q(register_10_q), .clk(clk));  // open: clr
  Register register_11 (.D(D7D6___________D0), .en(decoder_1_out10), .Q(register_11_q), .clk(clk));  // open: clr
  Register register_12 (.D(D7D6___________D0), .en(decoder_1_out11), .Q(register_12_q), .clk(clk));  // open: clr
  Register register_13 (.D(D7D6___________D0), .en(decoder_1_out12), .Q(register_13_q), .clk(clk));  // open: clr
  Register register_14 (.D(D7D6___________D0), .en(decoder_1_out13), .Q(register_14_q), .clk(clk));  // open: clr
  Register register_15 (.D(D7D6___________D0), .en(decoder_1_out14), .Q(register_15_q), .clk(clk));  // open: clr
  Register register_16 (.D(D7D6___________D0), .en(decoder_1_out15), .Q(register_16_q), .clk(clk));  // open: clr
  Hex_Digit_Display hex_digit_display_3 (.value(Output[7:4]));  // open: dp
  Multiplexer #(.select(4), .width(8)) multiplexer_1 (
    .in0(register_1_q), .in1(register_2_q), .in2(register_3_q), .in3(register_4_q), .in4(register_5_q),
    .in5(register_6_q), .in6(register_7_q), .in7(register_8_q), .in8(register_9_q), .in9(register_10_q),
    .in10(register_11_q), .in11(register_12_q), .in12(register_13_q), .in13(register_14_q),
    .in14(register_15_q), .in15(register_16_q), .out(Output), .sel(S3S2S1S0), .en(R_W_prime));
  Hex_Digit_Display hex_digit_display_4 (.value(Output[3:0]));  // open: dp

  // Notes on the sheet:
  //   R0
  //   R1
  //   R2
  //   R3
  //   R4
  //   R5
  //   R6
  //   R7
  //   R8
  //   R9
  //   Ra
  //   Rb
  //   Rc
  //   Rd
  //   Re
  //   Rf
endmodule

module PSW (
  input  [15:0] ALU,
  input  [7:0] A,
  input  [7:0] B,
  input  interupt,
  output Zero,
  output Overflow,
  output Carry,
  output Sign,
  output Even_Parity,
  output odd_parity,
  output Half_Carry,
  output Interupt_Flag
);

  Comparator #(.width(16)) comparator_1 (.a(ALU), .b({16{1'b0}}), .eq(Zero));  // open: gt, lt
  Comparator comparator_2 (.a(ALU[15:8]), .b({8{1'b0}}), .gt(Carry));  // open: eq, lt
  xor odd_parity_1 (odd_parity, ALU[0], ALU[1], ALU[2], ALU[3], ALU[4], ALU[5], ALU[6], ALU[7], ALU[9], ALU[10], ALU[11], ALU[12], ALU[13], ALU[14], ALU[15]);
  BitSelector bitselector_1 (.in(ALU[7:0]), .out(Sign), .sel(3'b111));
  not not_1 (Even_Parity, odd_parity);
  Adder #(.width(4)) adder_1 (.a(A[3:0]), .b(B[3:0]), .cout(Half_Carry));  // open: out, cin

  assign Interupt_Flag = interupt;
  assign Overflow = Carry;
endmodule
