// Logisim project coa-processor-cu.circ as structural Verilog: 1 circuit, main circuit main
module main (
  input  Clock,
  input  Reset,
  output PC_enable,
  output Mem_read,
  output IR,
  output Operand_fetch,
  output ALU,
  output R_W_prime
);

  wire [2:0] counter_1_q;

  Counter #(.width(3), .max('h7)) counter_1 (.Q(counter_1_q), .clk(Clock), .clr(Reset));  // open: load, D, count, carry
  Decoder #(.select(3), .enable("false")) decoder_1 (
    .out0(PC_enable), .out1(Mem_read), .out2(IR), .out3(Operand_fetch), .out4(ALU), .out5(R_W_prime),
    .sel(counter_1_q));  // open: out6, out7
endmodule
