// Logisim project coa-processor-pc.circ as structural Verilog: 1 circuit, main circuit main
module main (
  input  [7:0] PC_in,
  input  PC_enable,
  input  Reset,
  input  Clock,
  output [7:0] PC_out
);

  wire [7:0] adder_1_out;

  Adder adder_1 (.a(PC_in), .b(PC_out), .out(adder_1_out));  // open: cin, cout
  Hex_Digit_Display hex_digit_display_1 (.value(PC_out[7:4]));  // open: dp
  Register register_1 (.D(adder_1_out), .en(PC_enable), .Q(PC_out), .clk(Clock), .clr(Reset));
  Hex_Digit_Display hex_digit_display_2 (.value(PC_out[3:0]));  // open: dp
endmodule
