// Logisim project coa-processor-psw.circ as structural Verilog: 1 circuit, main circuit main
module main (
  input  [15:0] ALU,
  input  [7:0] A,
  input  [7:0] B,
  input  interupt,
  output Zero,
  output Overflow,
  output Carry,
  output Sign,
  output Even_Parity,
  output odd_parity,
  output Half_Carry,
  output Interupt_Flag
);

  Comparator #(.width(16)) comparator_1 (.a(ALU), .b({16{1'b0}}), .eq(Zero));  // open: gt, lt
  Comparator comparator_2 (.a(ALU[15:8]), .b({8{1'b0}}), .gt(Carry));  // open: eq, lt
  xor odd_parity_1 (odd_parity, ALU[0], ALU[1], ALU[2], ALU[3], ALU[4], ALU[5], ALU[6], ALU[7], ALU[9], ALU[10], ALU[11], ALU[12], ALU[13], ALU[14], ALU[15]);
  BitSelector bitselector_1 (.in(ALU[7:0]), .out(Sign), .sel(3'b111));
  not not_1 (Even_Parity, odd_parity);
  Adder #(.width(4)) adder_1 (.a(A[3:0]), .b(B[3:0]), .cout(Half_Carry));  // open: out, cin

  assign Interupt_Flag = interupt;
  assign Overflow = Carry;
endmodule
